# Fritzing sketch FFF (saved by Fritzing 0.9.9b)
perfboards: 1

parts:
  J12 = male pin header, 20 pins [form="♂ (male)"]
  J13 = male pin header, 20 pins [form="♂ (male)"]
  J14 = male pin header, 3 pins [form="♂ (male)"]
  J15 = male pin header, 4 pins [form="♂ (male)"]
  J16 = male pin header, 2 pins [form="♂ (male)"]
  J18 = male pin header, 8 pins [form="♂ (male)"]
  J19 = male pin header, 6 pins [form="♂ (male)"]
  J20 = screw terminal, 2 pins
  J21 = male pin header, 4 pins [form="♂ (male)"]
  RHT1 = Humidity and Temperature Sensor RHT03
  R1 = Resistor [tolerance=±5% power=0.25 resistance=10k package=THT]
  J17 = male pin header, 7 pins [form="♂ (male)"]

nets:
  N1: J12.pin1, J16.pin2
  N2: J12.pin2, J16.pin1
  N3: J12.pin4, J18.pin5, J19.pin4, J21.pin2
  N4: J12.pin5, J18.pin4, J19.pin3, J21.pin1
  N5: J12.pin6, RHT1.GND_1
  N6: J13.pin1, J17.pin1
  N7: J13.pin2, J17.pin2
  N8: J13.pin3, J18.pin1, J18.pin7, J19.pin5, J21.pin3
  N9: J13.pin4, J17.pin3
  N10: J13.pin5, J17.pin4
  N11: J13.pin6, J17.pin5
  N12: J13.pin7, J17.pin6
  N13: J13.pin9, J15.pin1
  N14: J13.pin11, J15.pin2
  N15: J13.pin12, J15.pin3
  N16: J13.pin14, J15.pin4
  N17: J13.pin16, J18.pin8, J19.pin6, J21.pin4, RHT1.Vcc, R1.Pin_0
  N18: J13.pin18, J14.pin1, J20.pin2
  N19: J13.pin20, J14.pin3, J19.pin2
  N20: RHT1.Data-signal, R1.Pin_1

notes:
  Cyan-Leitungen sind nicht als Kabel sondern als Lötsstellen auf der Unterseite der Platine zu bereachten
